# Fritzing sketch Schematics (saved by Fritzing 0.9.9b)
breadboards: 1

parts:
  Arduino_Uno = Arduino Uno (Rev3)
  GY-521 = InvenSense MPU6050
  HC-SR04 = HC-SR04 Ultrasonic Distance Sensor
  DHT11 = Humidity and Temperature Sensor RHT03

nets:
  GND: Arduino_Uno.GND, GY-521.GND, HC-SR04.GND, DHT11.GND_2
  N1: Arduino_Uno.D2, HC-SR04.TRIG
  N2: Arduino_Uno.D3_PWM, HC-SR04.ECHO
  N3: Arduino_Uno.D4, DHT11.Data-signal
  VCC: Arduino_Uno.5V, GY-521.VCC, HC-SR04.VCC, DHT11.Vcc
